# Fritzing sketch attiny1 (saved by Fritzing 0.9.10b)
breadboards: 1

parts:
  C2 = Ceramic Capacitor [capacitance=100nF voltage=35V package="100 mil [THT, multilayer]"]
  Bauteil4 = SMD Adapter
  R7 = Resistor [tolerance=±5% power=0.25 resistance=220 package=THT]
  LED1 = LED - 5mm [color="Red (635nm)" current=0.030 package="5 mm [THT]"]
  Bauteil5 = MPLAB Snap In-Circuit Debugger [part_number=PG164100]
  R8 = Resistor [tolerance=±5% power=0.25W resistance=10k package=THT]
  R9 = Resistor [tolerance=±5% power=0.25 resistance=220 package=THT]
  LED2 = LED - 5mm [color="Green (555nm)" current=0.030 package="5 mm [THT]"]
  JACK1 = 2.1mm Barrel Jack with Terminal Block

nets:
  N1: C2.0, Bauteil4.pin1, Bauteil5.TVDD, R8.Pin_0, JACK1.POS
  N2: C2.1, Bauteil4.pin_8, LED1.cathode, Bauteil5.GND, LED2.cathode, JACK1.NEG
  N3: Bauteil4.pin_4, R9.Pin_0
  N4: Bauteil4.pin_5, R7.Pin_0
  N5: Bauteil4.pin_6, Bauteil5.PGD, R8.Pin_1
  N6: R7.Pin_1, LED1.anode
  N7: R9.Pin_1, LED2.anode

notes:
  ATtiny212
  *
  * siehe ETN36
  5 V

custom parts:
  SMD Adapter: SMD Adapter SO8 SOIC8 SOP
